# Fritzing sketch Kodi-Monitor (saved by Fritzing 0.9.2b)
circuit board: 8.46667cm x 5.64444cm

parts:
  Raspberry_Pi_B_rev1 = Raspberry Pi B rev1
  21-Enter = Round Pushbutton
  4-Left = Round Pushbutton
  15-Down = Round Pushbutton
  17-Right = Round Pushbutton
  14-Up = Round Pushbutton
  18-Back = Round Pushbutton
  U1 = Graphical LCD 128x64 [package=lcd-g12864]  # not connected
  Power_plug1 = Power plug  # not connected

nets (from the schematic view):
  N1: Raspberry_Pi_B_rev1.5V, Raspberry_Pi_B_rev1.GPIO_15, 21-Enter.leg1, 4-Left.leg1, 15-Down.leg0, 15-Down.leg1, 17-Right.leg1, 14-Up.leg0, 18-Back.leg0
  N2: Raspberry_Pi_B_rev1.GPIO_14, 14-Up.leg1
  N3: Raspberry_Pi_B_rev1.GPIO_18, 18-Back.leg1
  N4: Raspberry_Pi_B_rev1.GPIO_21, 17-Right.leg0
  N5: Raspberry_Pi_B_rev1.GPIO_22, 21-Enter.leg0
  N6: Raspberry_Pi_B_rev1.GPIO_4, 4-Left.leg0
